// Logisim project test.circ as structural Verilog: 1 circuit, main circuit main
module main (
  input  RST,
  input  CLK,
  input  WE,
  input  [12:0] ADDR,
  input  [15:0] DATA_IN,
  output [15:0] DATA_OUT
);

  // HACK_Video_Display hack_video_display_1: pin names not known; wires that end beside it: RST, CLK, WE, ADDR, DATA_IN, DATA_OUT
endmodule
